# Fritzing sketch MicroCC300_DHT (saved by Fritzing 0.9.1b)
breadboards: 1

parts:
  CC3K1 = Adafruit CC3000 WiFi Breakout
  Part1 = Arduino Micro (Rev3)  # not connected
  DHT1 = DHT22 Humidity and Temperature Sensor
  R1 = Resistor [tolerance=±5% resistance=220 package="0603 [SMD]"]

nets:
  GND: CC3K1.GND, DHT1.GND
  VIN: CC3K1.VIN, DHT1.VDD, R1.Pin_0
  N1: CC3K1.TXD, CC3K1.RXD
  N2: DHT1.DATA, R1.Pin_1

custom parts:
  Adafruit CC3000 WiFi Breakout: CC3000 WiFi Breakout
